// Logisim project 8bit-cpu.circ as structural Verilog: 7 circuits, main circuit main
module main (
);

  wire and_1_out, clock_1_out, clock_2_out, clock_3_out, controlunit_module_1_pc_load,
       controlunit_module_1_stack_re, controlunit_module_1_wreg_we;
  wire [7:0] adder_1_out, controlled_buffer_1_out, multiplexer_1_out, PC_q;
  wire [12:0] rom_module_1_data;

  Adder adder_1 (.a(PC_q), .b(8'h1), .out(adder_1_out));  // open: cin, cout
  Multiplexer #(.width(8)) multiplexer_1 (
    .in0(adder_1_out), .in1(PC_q), .out(multiplexer_1_out), .sel(controlunit_module_1_stack_re));
  Register PC (.D(multiplexer_1_out), .clk(clock_1_out), .Q(PC_q));  // open: en, clr
  Clock clock_1 (.out(clock_1_out));
  ROM_module rom_module_1 (.addr(PC_q), .data(rom_module_1_data));
  and and_1 (and_1_out, clock_2_out, controlunit_module_1_pc_load);
  Clock clock_2 (.out(clock_2_out));
  assign controlled_buffer_1_out = and_1_out ? rom_module_1_data[7:0] : 8'bz;  // Controlled_Buffer controlled_buffer_1
  ControlUnit_module controlunit_module_1 (
    .operand(controlled_buffer_1_out), .opcode(rom_module_1_data[12:8]),
    .Wreg_WE(controlunit_module_1_wreg_we), .PC_LOAD(controlunit_module_1_pc_load),
    .STACK_RE(controlunit_module_1_stack_re), .HALT(controlunit_module_1_stack_re));  // open: zeroF, carryF, WREG_RE, REG_WE, REG_SEL, RAM_RE, RAM_WE, RAM_ADDR_EN, ALU_OP, ALU_EN, PC_EN, SP_INC, SP_DEC, STACK_WE
  Register Wreg (.en(controlunit_module_1_wreg_we), .clk(clock_3_out));  // open: D, Q, clr
  Clock clock_3 (.out(clock_3_out));

  // Notes on the sheet:
  //   DATABUS
endmodule

module ALU (
  input  ALUOP2,
  input  ALUOP1,
  input  ALUOP0,
  input  [7:0] Wreg,
  input  [7:0] Rn,
  output [7:0] Result,
  output carryF,
  output zeroF
);

  wire and_2_out, and_3_out, and_4_out, not_3_out, not_4_out, xor_2_out;
  wire [7:0] adder_1_out, adder_2_out, and_1_out, multiplexer_1_out, multiplexer_2_out, multiplexer_3_out,
       multiplexer_4_out, not_1_out, not_2_out, or_1_out, xor_1_out;

  assign not_1_out = ~Wreg;  // NOT_Gate not_1, 8 bits wide
  Adder adder_1 (.a(8'h1), .b(not_2_out), .out(adder_1_out));  // open: cin, cout
  assign not_2_out = ~Rn;  // NOT_Gate not_2, 8 bits wide
  assign and_1_out = Wreg & Rn;  // AND_Gate and_1, 8 bits wide
  assign or_1_out = Wreg | Rn;  // OR_Gate or_1, 8 bits wide
  assign xor_1_out = Wreg ^ Rn;  // XOR_Gate xor_1, 8 bits wide
  and and_2 (and_2_out, ALUOP1, ALUOP2);
  Multiplexer #(.width(8)) multiplexer_1 (.in0(Rn), .in1(adder_1_out), .out(multiplexer_1_out), .sel(ALUOP0));
  Multiplexer #(.width(8)) multiplexer_2 (.in0(8'h1), .in1({8{1'b1}}), .out(multiplexer_2_out), .sel(ALUOP0));
  Multiplexer #(.width(8)) multiplexer_3 (
    .in0(multiplexer_1_out), .in1(multiplexer_2_out), .out(multiplexer_3_out), .sel(and_2_out));
  not not_3 (not_3_out, ALUOP1);
  not not_4 (not_4_out, ALUOP2);
  Adder adder_2 (.a(Wreg), .b(multiplexer_3_out), .out(adder_2_out), .cout(carryF));  // open: cin
  and and_3 (and_3_out, not_3_out, ALUOP2);
  and and_4 (and_4_out, ALUOP1, not_4_out);
  xor xor_2 (xor_2_out, and_3_out, and_4_out);
  Multiplexer #(.select(3), .width(8)) multiplexer_4 (
    .in2(and_1_out), .in3(or_1_out), .in4(xor_1_out), .in5(not_1_out), .out(multiplexer_4_out),
    .sel({ALUOP2, ALUOP1, ALUOP0}));  // open: in0, in1, in6, in7
  Multiplexer #(.width(8)) multiplexer_5 (.in0(adder_2_out), .in1(multiplexer_4_out), .out(Result), .sel(xor_2_out));
  Comparator comparator_1 (.a({8{1'b0}}), .b(adder_2_out), .eq(zeroF));  // open: gt, lt
endmodule

module ROM_module (
  input  [7:0] addr,
  output [12:0] data
);

  ROM #(.dataWidth(13)) rom_1 (.addr(addr), .data(data));

  // Notes on the sheet:
  //   contents of rom_1 (hex, n*v repeats v):
  //   105 500 900 400 1300 1300
endmodule

module RAM_module (
  input  [7:0] addr,
  input  [7:0] dataIn,
  input  readEnable,
  input  writeEnable,
  input  clk,
  output [7:0] dataOut
);

  wire [7:0] ram_1_dout;

  RAM ram_1 (.addr(addr), .we(writeEnable), .oe(readEnable), .clk(clk), .din(dataIn), .dout(ram_1_dout));
  assign dataOut = readEnable ? ram_1_dout : 8'bz;  // Controlled_Buffer controlled_buffer_1
endmodule

module Registers_Module (
  input  [2:0] readSelect,
  input  [7:0] dataIn,
  input  clk,
  input  clear,
  input  [2:0] writeSelect,
  input  writeEnable,
  output [7:0] dataOut
);

  wire decoder_1_out0, decoder_1_out1, decoder_1_out2, decoder_1_out3, decoder_1_out4, decoder_1_out5,
       decoder_1_out6, decoder_1_out7;
  wire [7:0] MA_q, MD_q, R0_q, R1_q, R2_q, R3_q, SP_q, Wreg_q;

  Decoder #(.select(3)) decoder_1 (
    .out0(decoder_1_out0), .out1(decoder_1_out1), .out2(decoder_1_out2), .out3(decoder_1_out3),
    .out4(decoder_1_out4), .out5(decoder_1_out5), .out6(decoder_1_out6), .out7(decoder_1_out7),
    .sel(writeSelect), .en(writeEnable));
  Register Wreg (.D(dataIn), .en(decoder_1_out0), .clk(clk), .Q(Wreg_q), .clr(clear));
  Register R0 (.D(dataIn), .en(decoder_1_out1), .clk(clk), .Q(R0_q), .clr(clear));
  Register R1 (.D(dataIn), .en(decoder_1_out2), .clk(clk), .Q(R1_q), .clr(clear));
  Register R2 (.D(dataIn), .en(decoder_1_out3), .clk(clk), .Q(R2_q), .clr(clear));
  Register R3 (.D(dataIn), .en(decoder_1_out4), .clk(clk), .Q(R3_q), .clr(clear));
  Register SP (.D(dataIn), .en(decoder_1_out5), .clk(clk), .Q(SP_q), .clr(clear));
  Register MD (.D(dataIn), .en(decoder_1_out6), .clk(clk), .Q(MD_q), .clr(clear));
  Register MA (.D(dataIn), .en(decoder_1_out7), .clk(clk), .Q(MA_q), .clr(clear));
  Multiplexer #(.select(3), .width(8)) multiplexer_1 (
    .in0(Wreg_q), .in1(R0_q), .in2(R1_q), .in3(R2_q), .in4(R3_q), .in5(SP_q), .in6(MD_q), .in7(MA_q),
    .out(dataOut), .sel(readSelect));
endmodule

module ControlUnit_module (
  input  [7:0] operand,
  input  [4:0] opcode,
  input  zeroF,
  input  carryF,
  output Wreg_WE,
  output WREG_RE,
  output REG_WE,
  output [2:0] REG_SEL,
  output RAM_RE,
  output RAM_WE,
  output RAM_ADDR_EN,
  output [2:0] ALU_OP,
  output ALU_EN,
  output PC_LOAD,
  output PC_EN,
  output SP_INC,
  output SP_DEC,
  output STACK_WE,
  output STACK_RE,
  output HALT
);

  wire and_1_out, and_2_out, data_out, decoder_1_out0, decoder_1_out1, decoder_1_out4, decoder_1_out8,
       decoder_1_out9, decoder_1_out10, decoder_1_out11, decoder_1_out12, decoder_1_out13, decoder_1_out14,
       decoder_1_out15, decoder_1_out16, decoder_1_out17, decoder_1_out18, not_1_out, not_2_out, not_3_out,
       or_1_out, or_2_out, or_3_out, or_4_out, or_5_out, or_6_out, or_8_out, or_10_out, or_11_out, or_12_out,
       or_14_out;

  Decoder #(.select(5)) decoder_1 (
    .out0(decoder_1_out0), .out1(decoder_1_out1), .out2(RAM_RE), .out3(RAM_WE), .out4(decoder_1_out4),
    .out5(REG_WE), .out6(SP_INC), .out7(SP_DEC), .out8(decoder_1_out8), .out9(decoder_1_out9),
    .out10(decoder_1_out10), .out11(decoder_1_out11), .out12(decoder_1_out12), .out13(decoder_1_out13),
    .out14(decoder_1_out14), .out15(decoder_1_out15), .out16(decoder_1_out16), .out17(decoder_1_out17),
    .out18(decoder_1_out18), .out19(HALT), .sel(opcode));  // open: out20, out21, out22, out23, out24, out25, out26, out27, out28, out29, out30, out31, en
  not not_1 (not_1_out, opcode[4]);
  not not_2 (not_2_out, opcode[3]);
  not not_3 (not_3_out, opcode[4]);
  and ALU (ALU_EN, opcode[3], not_1_out);
  and data (data_out, not_2_out, not_3_out);
  or or_1 (or_1_out, decoder_1_out9, decoder_1_out10);
  or or_2 (or_2_out, decoder_1_out11, decoder_1_out12);
  or or_3 (or_3_out, decoder_1_out4, REG_WE);
  or or_4 (or_4_out, or_1_out, or_2_out);
  or or_5 (or_5_out, decoder_1_out8, or_4_out);
  and and_1 (and_1_out, decoder_1_out17, zeroF);
  and and_2 (and_2_out, decoder_1_out18, carryF);
  or or_6 (or_6_out, or_3_out, or_5_out);
  or or_7 (RAM_ADDR_EN, RAM_RE, RAM_WE);
  or or_8 (or_8_out, and_1_out, and_2_out);
  assign REG_SEL = or_6_out ? operand[2:0] : 3'bz;  // Controlled_Buffer rn_address
  or or_9 (PC_LOAD, decoder_1_out16, or_8_out);
  or or_10 (or_10_out, RAM_WE, REG_WE);
  or or_11 (or_11_out, decoder_1_out1, RAM_RE);
  or or_12 (or_12_out, decoder_1_out4, SP_DEC);
  or or_13 (WREG_RE, or_10_out, SP_INC);
  or or_14 (or_14_out, or_11_out, or_12_out);
  or or_15 (Wreg_WE, or_14_out, ALU_EN);
  or or_16 (PC_EN, ALU_EN, data_out);

  assign ALU_OP = opcode[2:0];
  assign STACK_RE = SP_DEC;
  assign STACK_WE = SP_INC;

  // Notes on the sheet:
  //   Rn address bus
  //   SUB
  //   AND
  //   OR
  //   XOR
  //   NOT
  //   INC
  //   DEC
  //   JMP
  //   JZ
  //   JC
  //   STORE
  //   POP
  //   ADD
  //   HALT
  //   LOADI
  //   LOADA
  //   MOV
  //   MOVW
  //   PUSH
  //   NOP
endmodule

module testing_WREG (
);

  wire alu_1_carryf, alu_1_zerof, and_1_out, clock_1_out, clock_2_out, clock_3_out, clock_4_out,
       controlled_buffer_2_out, controlled_buffer_3_out, controlunit_module_1_alu_en,
       controlunit_module_1_halt, controlunit_module_1_pc_en, controlunit_module_1_reg_we,
       controlunit_module_1_wreg_we, decoder_1_out1, decoder_1_out2, decoder_1_out3, decoder_1_out4,
       decoder_1_out5, decoder_1_out6, decoder_1_out16, decoder_1_out17, decoder_1_out18, or_1_out, or_2_out;
  wire [2:0] controlunit_module_1_alu_op, controlunit_module_1_reg_sel;
  wire [7:0] adder_1_out, alu_1_result, controlled_buffer_1_out, multiplexer_1_out, PC_q,
       registers_module_1_dataout, ROM_TO_DATABUS_out, Wreg_q;
  wire [12:0] rom_module_1_data;

  Adder adder_1 (.a(PC_q), .b(8'h1), .out(adder_1_out));  // open: cin, cout
  Multiplexer #(.width(8)) multiplexer_1 (
    .in0(adder_1_out), .in1(PC_q), .out(multiplexer_1_out), .sel(controlunit_module_1_halt));
  Clock clock_1 (.out(clock_1_out));
  Register PC (.D(multiplexer_1_out), .clk(clock_1_out), .Q(PC_q));  // open: en, clr
  ROM_module rom_module_1 (.addr(PC_q), .data(rom_module_1_data));
  and and_1 (and_1_out, clock_2_out, controlunit_module_1_pc_en);
  Clock clock_2 (.out(clock_2_out));
  assign controlled_buffer_1_out = and_1_out ? rom_module_1_data[7:0] : 8'bz;  // Controlled_Buffer controlled_buffer_1
  assign ROM_TO_DATABUS_out = or_1_out ? rom_module_1_data[7:0] : 8'bz;  // Controlled_Buffer ROM_TO_DATABUS
  ControlUnit_module controlunit_module_1 (
    .operand(controlled_buffer_1_out), .opcode(rom_module_1_data[12:8]), .zeroF(controlled_buffer_2_out),
    .carryF(controlled_buffer_3_out), .Wreg_WE(controlunit_module_1_wreg_we),
    .REG_WE(controlunit_module_1_reg_we), .REG_SEL(controlunit_module_1_reg_sel),
    .ALU_OP(controlunit_module_1_alu_op), .ALU_EN(controlunit_module_1_alu_en),
    .PC_EN(controlunit_module_1_pc_en), .HALT(controlunit_module_1_halt));  // open: WREG_RE, RAM_RE, RAM_WE, RAM_ADDR_EN, PC_LOAD, SP_INC, SP_DEC, STACK_WE, STACK_RE
  Clock clock_3 (.out(clock_3_out));
  Register Wreg (
    .D(ROM_TO_DATABUS_out), .en(controlunit_module_1_wreg_we), .clk(clock_4_out), .Q(Wreg_q));  // open: clr
  Clock clock_4 (.out(clock_4_out));
  Registers_Module registers_module_1 (
    .readSelect(controlunit_module_1_reg_sel), .dataIn(Wreg_q), .clk(clock_3_out),
    .writeSelect(controlunit_module_1_reg_sel), .writeEnable(controlunit_module_1_reg_we),
    .dataOut(registers_module_1_dataout));  // open: clear
  Decoder #(.select(5)) decoder_1 (
    .out1(decoder_1_out1), .out2(decoder_1_out2), .out3(decoder_1_out3), .out4(decoder_1_out4),
    .out5(decoder_1_out5), .out6(decoder_1_out6), .out16(decoder_1_out16), .out17(decoder_1_out17),
    .out18(decoder_1_out18), .sel(rom_module_1_data[12:8]));  // open: out0, out7, out8, out9, out10, out11, out12, out13, out14, out15, out19, out20, out21, out22, out23, out24, out25, out26, out27, out28, out29, out30, out31, en
  assign ROM_TO_DATABUS_out = or_2_out ? Wreg_q : 8'bz;  // Controlled_Buffer WREG_TO_DATABUS
  assign ROM_TO_DATABUS_out = decoder_1_out4 ? registers_module_1_dataout : 8'bz;  // Controlled_Buffer RN_TO_DATABUS
  or or_1 (or_1_out, decoder_1_out1, decoder_1_out2, decoder_1_out16, decoder_1_out17, decoder_1_out18);
  ALU alu_1 (
    .ALUOP2(controlunit_module_1_alu_op[2]), .ALUOP1(controlunit_module_1_alu_op[1]),
    .ALUOP0(controlunit_module_1_alu_op[0]), .Wreg(Wreg_q), .Rn(registers_module_1_dataout),
    .Result(alu_1_result), .carryF(alu_1_carryf), .zeroF(alu_1_zerof));
  or or_2 (or_2_out, decoder_1_out3, decoder_1_out5, decoder_1_out6);
  assign controlled_buffer_2_out = controlunit_module_1_alu_en ? alu_1_zerof : 1'bz;  // Controlled_Buffer controlled_buffer_2
  assign ROM_TO_DATABUS_out = controlunit_module_1_alu_en ? alu_1_result : 8'bz;  // Controlled_Buffer ALU_ENABLE_CONTROLLER
  assign controlled_buffer_3_out = controlunit_module_1_alu_en ? alu_1_carryf : 1'bz;  // Controlled_Buffer controlled_buffer_3

  // Notes on the sheet:
  //   DATABUS
endmodule
